# Fritzing sketch Official_PCB (saved by Fritzing 0.9.3b)
circuit board: 8.4cm x 5cm
breadboards: 1

parts:
  J4 = female pin header, 6 pins [form="♀ (female)"]
  J3 = female pin header, 6 pins [form="♀ (female)"]
  J5 = female pin header, 6 pins [form="♀ (female)"]
  J1 = female pin header, 6 pins [form="♀ (female)"]
  J7 = female pin header, 6 pins [form="♀ (female)"]
  J8 = female pin header, 10 pins [form="♀ (female)"]  # not connected
  J9 = female pin header, 10 pins [form="♀ (female)"]  # not connected
  J2 = female pin header, 2 pins [form="♀ (female)"]
  J6 = female pin header, 2 pins [form="♀ (female)"]
  J10 = female pin header, 15 pins [form="♀ (female)"]
  J11 = female pin header, 15 pins [form="♀ (female)"]
  J13 = female pin header, 1 pin [form="♀ (female)"]
  J14 = female pin header, 1 pin [form="♀ (female)"]
  J12 = female pin header, 1 pin [form="♀ (female)"]

nets:
  N1: J4.pin1, J11.pin4
  N2: J4.pin2, J11.pin5
  N3: J4.pin3, J3.pin3, J5.pin3, J2.pin1, J10.pin15
  N4: J4.pin5, J11.pin6
  N5: J4.pin6, J11.pin7
  N6: J3.pin1, J10.pin1
  N7: J3.pin2, J11.pin1
  N8: J3.pin5, J11.pin2
  N9: J3.pin6, J11.pin3
  N10: J5.pin1, J11.pin10
  N11: J5.pin2, J11.pin11
  N12: J5.pin5, J11.pin14
  N13: J5.pin6, J11.pin15
  N14: J1.pin1, J10.pin9
  N15: J1.pin2, J10.pin8
  N16: J1.pin3, J10.pin7
  N17: J1.pin4, J10.pin6
  N18: J1.pin5, J10.pin5
  N19: J1.pin6, J10.pin4
  N20: J7.pin1, J7.pin6, J2.pin2, J10.pin14, J13.pin1, J14.pin1, J12.pin1
  N21: J6.pin1, J11.pin9
  N22: J6.pin2, J11.pin8
