# Fritzing sketch micro_expend (saved by Fritzing 0.9.3b)
circuit board: 8.46667cm x 5.64444cm
perfboards: 1

parts:
  元件1 = Arduino Micro (Rev3)
  U2 = L9110 H-bridge module [part_number="L9110 H-bridge"]
  U3 = L9110 H-bridge module [part_number="L9110 H-bridge"]
  S1 = Toggle Switch [package=THT]  # not connected
  U1 = L9110 H-bridge module [part_number="L9110 H-bridge"]
  S2 = Toggle Switch [package=THT]  # not connected
  S3 = Toggle Switch [package=THT]  # not connected
  S4 = Toggle Switch [package=THT]  # not connected
  S5 = Toggle Switch [package=THT]  # not connected
  S6 = Toggle Switch [package=THT]  # not connected

nets:
  GND: 元件1.GND, U2.GND, U3.GND, U1.GND
  N1: 元件1.D6_PWM/A7, U2.A-IB
  N2: 元件1.D8_PWM/A8, U2.B-IB
  N3: 元件1.D9_PWM/A9, U3.A-IB
  N4: 元件1.D10_PWM/A10, U3.B-IB
  N5: 元件1.D11_PWM, U1.A-IB
  N6: 元件1.D12_PWM/A11, U1.B-IB
  VCC: 元件1.5V, U2.VCC, U3.VCC, U1.VCC
  N7: 元件1.A5, U2.A-IA
  N8: 元件1.A4, U2.B-IA
  N9: 元件1.A3, U3.A-IA
  N10: 元件1.A2, U3.B-IA
  N11: 元件1.A1, U1.A-IA
  N12: 元件1.A0, U1.B-IA
  N13: U1.MOTOR_A-A, U1.MOTOR_B-B
