# Fritzing sketch nano_expend (saved by Fritzing 0.9.3b)
perfboards: 1

parts:
  元件1 = Arduino Nano (Rev3.0)
  U1 = L9110 H-bridge module [part_number="L9110 H-bridge"]
  U2 = L9110 H-bridge module [part_number="L9110 H-bridge"]
  U3 = L9110 H-bridge module [part_number="L9110 H-bridge"]
  S1 = Toggle Switch [package=THT]
  S2 = Toggle Switch [package=THT]
  S3 = Toggle Switch [package=THT]
  S4 = Toggle Switch [package=THT]
  S5 = Toggle Switch [package=THT]
  S6 = Toggle Switch [package=THT]

nets:
  GND: 元件1.GND, U1.GND, U2.GND, U3.GND, S2.L2, S3.L2, S4.L2, S5.L2, S6.L2
  N1: 元件1.D2, U3.A-IA
  N2: 元件1.D3, U3.A-IB
  N3: 元件1.D4, U3.B-IA
  N4: 元件1.D5, U3.B-IB
  N5: 元件1.D6, U2.A-IB
  N6: 元件1.D7, U2.A-IA
  N7: 元件1.D8, U2.B-IA
  N8: 元件1.D9, U2.B-IB
  N9: 元件1.D10, U1.A-IB
  N10: 元件1.D11/MOSI, U1.B-IB
  N11: 元件1.D12/MISO, U1.A-IA
  VCC: 元件1.5V, U1.VCC, U3.VCC
  N12: 元件1.A5, S6.L1
  N13: 元件1.A4, S5.L1
  N14: 元件1.A3, S4.L1
  N15: 元件1.A2, S3.L1
  N16: 元件1.A1, S2.L1
  N17: 元件1.A0, S1.L1
  N18: 元件1.D13/SCK, U1.B-IA
  N19: S1.COM, S6.COM
