# Fritzing sketch micro_expend (saved by Fritzing 0.9.3b)

parts:
  元件1 = Arduino Micro (Rev3)
  U1 = L9110 H-bridge module [part_number="L9110 H-bridge"]
  U2 = L9110 H-bridge module [part_number="L9110 H-bridge"]
  U3 = L9110 H-bridge module [part_number="L9110 H-bridge"]
  S1 = Toggle Switch [package=THT]
  S2 = Toggle Switch [package=THT]
  S3 = Toggle Switch [package=THT]
  S4 = Toggle Switch [package=THT]
  S5 = Toggle Switch [package=THT]
  S6 = Toggle Switch [package=THT]

nets:
  N1: 元件1.D1/TX, U1.A-IA
  N2: 元件1.D0/RX, U1.B-IA
  GND: 元件1.GND, U1.GND, U2.GND, U3.GND, S1.COM, S2.COM, S3.COM, S4.COM, S5.COM, S6.COM
  N3: 元件1.D4_PWM/A6, U1.A-IB
  N4: 元件1.D5_PWM, U1.B-IB
  N5: 元件1.D6_PWM/A7, U2.A-IB
  N6: 元件1.D7, U2.B-IB
  N7: 元件1.D8_PWM/A8, U2.A-IA
  N8: 元件1.D9_PWM/A9, U2.B-IA
  N9: 元件1.D10_PWM/A10, U3.A-IB
  N10: 元件1.D11_PWM, U3.A-IA
  N11: 元件1.D12_PWM/A11, U3.B-IB
  VCC: 元件1.5V, U1.VCC, U2.VCC, U3.VCC
  N12: 元件1.A5, S5.L1
  N13: 元件1.A4, S6.L1
  N14: 元件1.A3, S4.L1
  N15: 元件1.A2, S1.L1
  N16: 元件1.A1, S3.L1
  N17: 元件1.A0, S2.L1
  N18: 元件1.D13_PWM, U3.B-IA
